// Logisim project proiect_bun1.circ as structural Verilog
module main (
  input  reset,
  input  invers,
  input  clk,
  input  PD,
  input  PC,
  output is_left,
  output [3:0] Anozi,
  output [6:0] Catozi
);

  wire divizor_frecventa_de_200hz_1_clk_out, ps2_reader_1_buton_dreapta, ps2_reader_1_buton_stanga,
       uc_1_down, uc_1_up;
  wire [3:0] numarator_1_counterout1, numarator_1_counterout2, numarator_1_counterout3;

  PS2_READER ps2_reader_1 (
    .clock(clk), .reset(reset), .PD(PD), .PC(PC), .buton_stanga(ps2_reader_1_buton_stanga),
    .buton_dreapta(ps2_reader_1_buton_dreapta));
  divizor_frecventa_de_200Hz divizor_frecventa_de_200hz_1 (
    .clk_in(clk), .clk_out(divizor_frecventa_de_200hz_1_clk_out));
  uc uc_1 (
    .buton_stanga(ps2_reader_1_buton_stanga), .buton_dreapta(ps2_reader_1_buton_dreapta), .reset(reset),
    .invers(invers), .clk(clk), .is_left(is_left), .up(uc_1_up), .down(uc_1_down));
  numarator numarator_1 (
    .clk(clk), .up(uc_1_up), .down(uc_1_down), .reset(reset), .counterout1(numarator_1_counterout1),
    .counterout2(numarator_1_counterout2), .counterout3(numarator_1_counterout3));
  ssd ssd_1 (
    .n1(numarator_1_counterout1), .n2(numarator_1_counterout2), .n3(numarator_1_counterout3),
    .CLK(divizor_frecventa_de_200hz_1_clk_out), .Anod(Anozi), .Catod(Catozi));
endmodule

// VHDL entity PS2_READER, as the project stores it:
library ieee;
use ieee.std_logic_1164.all;
use ieee.std_logic_unsigned.all;

entity PS2_READER is
    port (
        clock : in std_logic;
        reset : in std_logic;
        PD : in std_logic;
        PC : in std_logic;
        buton_stanga : out std_logic;
        buton_dreapta : out std_logic
    );
end PS2_READER;

architecture Behavioral of PS2_READER is
    signal biti_mouse : std_logic_vector(42 downto 0) := (others => '0');
    signal numar_biti_dati_mouse : std_logic_vector(5 downto 0) := (others => '0');
    signal plin : std_logic;
    signal stanga_apasat : std_logic := '0';
    signal dreapta_apasat : std_logic := '0';
 
begin
	--NUMARARE BITI
    process (reset, PC)
    begin
        if reset = '1' then
            numar_biti_dati_mouse <= (others => '0');
        elsif falling_edge(PC) then
            if numar_biti_dati_mouse <= 42 then
                numar_biti_dati_mouse <= numar_biti_dati_mouse + 1;
            else
                numar_biti_dati_mouse <= (others => '0');
            end if;
        end if;
    end process;

    process (PC, reset)
    begin
        plin <= '0';
        if reset = '1' then
            biti_mouse <= (others => '0');
        elsif falling_edge(PC) then
            biti_mouse <= biti_mouse(41 downto 0) & PD;
            if numar_biti_dati_mouse = 42 then
                plin <= '1';
            end if;
        end if;
    end process;

    process (clock)
    begin
        if rising_edge(clock) then    
            buton_stanga <= '0';
            buton_dreapta <= '0';
            
            if plin = '1' then

                if biti_mouse(41) = '1' and stanga_apasat = '0' then
                    buton_stanga <= '1';
                elsif biti_mouse(40) = '1' and dreapta_apasat = '0' then
                    buton_dreapta <= '1';
                end if;
                stanga_apasat <= biti_mouse(41);
                dreapta_apasat <= biti_mouse(40);
            end if;    
        end if;
    end process;
end Behavioral;

// VHDL entity numarator, as the project stores it:
LIBRARY ieee;
USE ieee.std_logic_1164.all;
USE ieee.std_logic_unsigned.all;

ENTITY numarator IS
  PORT (
    clk: in std_logic;
    up, down: in std_logic;
    reset: in std_logic;
    --load: in std_logic;
    --clear: in std_logic;
    counterout1: out std_logic_vector (3 DOWNTO 0);
    counterout2: out std_logic_vector (3 DOWNTO 0);
    counterout3: out std_logic_vector (3 DOWNTO 0)
    --carry, borrow: out std_logic
  );
END numarator;

ARCHITECTURE Structural OF numarator IS
  signal inceput: std_logic_vector (3 downto 0) := "0000";
  signal ok  : std_logic := '0';
  signal okd  : std_logic := '0';
  signal oprit: std_logic_vector (3 downto 0) := "1001";
  signal val1 : std_logic_vector (3 downto 0) := "0000";
  signal val2 : std_logic_vector (3 downto 0) := "0000";
  signal val3 : std_logic_vector (3 downto 0) := "0000";
BEGIN
  process(clk,reset)
    variable c: std_logic_vector (3 downto 0) := "0000";
    variable c1: std_logic_vector (3 downto 0) := "0000";
    variable c2: std_logic_vector (3 downto 0) := "0000";
    variable stop : std_logic := '0';
    variable stopd : std_logic := '0';
  begin
  if reset = '1' then
		c2 := "0000";
          c1 := "0000";
          c := "0000";
          val1 <= c;
          val2 <= c1;
         	val3 <= c2;
  else
    if rising_edge(clk) then

      if stop = '0' then
        if up = '1' then
          if ok = '0' then
            ok <= '1';
            c := "0000";
            c1 := "0000";
          else
          
            c := c + 1;
            stopd := '0';
          end if;
        
        if c = "1010" then
            c := inceput;
          c1 := c1 + 1;
         val1 <= c;
          val2 <= c1;
          val3 <= c2;
          if c1 = "1010" then
          c2 := c2 + 1;
          c1 := inceput;
          c := inceput;
          val1 <= c;
          val2 <= c1;
         val3 <= c2;
          if c2 = "1010" then
          stop := '1';
          c2 := "1001";
          c1 := "1001";
          c := "1001";
          val1 <= c;
          val2 <= c1;
         val3 <= c2;
          end if;
         
            
          end if;
          ELSE
      val1 <= c;
      val2 <= c1;
      val3 <= c2;
        end if;
        end if;
      end if;
    

       
    if stopd = '0' then
        if down = '1' then
          if ok = '0' then
            ok <= '1';
            c := "0000";
            c1 := "0000";
          else
            c := c - 1;
            stop := '0';
          end if;
        
        if c = "1111" then
            c := oprit;
          c1 := c1 - 1;
         val1 <= c;
          val2 <= c1;
          val3 <= c2;
          if c1 = "1111" then
          c2 := c2 - 1;
          c1 := oprit;
          c := oprit;
          val1 <= c;
          val2 <= c1;
         val3 <= c2;
          if c2 = "1111" then
          stopd := '1';
          c2 := "0000";
          c1 := "0000";
          c := "0000";
          val1 <= c;
          val2 <= c1;
         val3 <= c2;
          end if;
         
            
          end if;
          ELSE
      val1 <= c;
      val2 <= c1;
      val3 <= c2;
        end if;
        end if;
      end if;


    end if;
    end if;
  end process;

  counterout1 <= val1;
  counterout2 <= val2;
  counterout3 <= val3;
END Structural;

// VHDL entity uc, as the project stores it:
LIBRARY ieee;
USE ieee.std_logic_1164.all;

ENTITY uc IS
  PORT (
  	buton_stanga: in std_logic;
  	buton_dreapta: in std_logic;
  	reset: in std_logic;
  	invers: in std_logic;
	clk: in std_logic;
	is_left:out std_logic;
	up: out std_logic;
	down: out std_logic
    );
END uc;


ARCHITECTURE behav OF uc IS

BEGIN

	process(clk,reset)
	begin
	if reset = '1' then
	up <= '0';
	down <= '0';
	else
	if rising_edge(clk) then
		if invers = '1' then
			is_left <= '0';
			if buton_stanga = '1' then
				down <= '1';
			else
				down <= '0';	
			end if;
			
			if buton_dreapta = '1' then
				up <= '1';
			else
				up <= '0';	
			end if;
		else
			is_left <= '1';
			if buton_stanga = '1' then
				up <= '1';
			else
				up <= '0';	
			end if;
			
			if buton_dreapta = '1' then
				down <= '1';
			else
				down <= '0';	
			end if;
				
			end if;
	end if;
	end if;
	end process;

END behav;

// VHDL entity ssd, as the project stores it:
LIBRARY ieee;
USE ieee.std_logic_1164.all;

USE ieee.std_logic_unsigned.all;

USE ieee.numeric_std.all;
ENTITY ssd IS
  PORT (
  	n1 : in std_logic_vector (3 downto 0);
  	n2 : in std_logic_vector (3 downto 0);
  	n3 : in std_logic_vector (3 downto 0);
  	CLK :  in std_logic;
  	Anod : out std_logic_vector (3 downto 0);
  	Catod : out std_logic_vector (6 downto 0)

  	--pozitie : out std_logic_vector (2 downto 0)
  
    );
END ssd;


ARCHITECTURE behav OF ssd IS

signal cat : std_logic_vector (6 downto 0) := "0000000";
signal ano : std_logic_vector (3 downto 0) := "0000";
signal poz : std_logic_vector (2 downto 0) := "000";
signal digit : std_logic_vector (3 downto 0) := "0000";


BEGIN


	process(CLK)
	begin
		if rising_edge(CLK) then
			poz <= poz +1;
		end if;
	end process;

	process(poz)	
		begin
			case poz is
				--when "00" =>
					--ano <= "1000";

				--when "01" =>
				--	ano <= "0100";
				when "001" =>
					ano <= "0100";
					digit <= n3;
				when "010" =>
					ano <= "0010";
					digit <= n2 ;
				when "011" =>
					ano <= "0001";
					digit <= n1;
				when others =>
					ano <= "0000";
					digit <= "1111";
				end case;
		end process;

	process(digit)
		begin
			case digit is
				when "0000" =>
					cat <= "0111111";
				when x"1" =>
					cat <= "0000110";
				when x"2" =>
					cat <= "1011011";
				when x"3" =>
					cat <= "1001111";
				when x"4" =>
					cat <= "1100110";
				when x"5" =>
					cat <= "1101101";
				when x"6" =>
					cat <= "1111101";
				when x"7" =>
					cat <= "0100111";
				when x"8" =>
					cat <= "1111111";
				when x"9" =>
					cat <= "1101111";
				when others =>
					cat <= "0000000";
			end case;
		end process;

	Anod <= ano ;
	Catod <= cat;

END behav;

// VHDL entity divizor_frecventa_de_200Hz, as the project stores it:
library IEEE;
use IEEE.STD_LOGIC_1164.ALL;

entity divizor_frecventa_de_200Hz is
    Port (
        clk_in : in  STD_LOGIC;
        clk_out: out STD_LOGIC
    );
end divizor_frecventa_de_200Hz;

architecture behav of divizor_frecventa_de_200Hz is
    signal temporal: STD_LOGIC;
    signal counter : integer range 0 to 124999 := 0;
begin
    process (clk_in) begin
        if rising_edge(clk_in) then
            if (counter = 124999) then
                temporal <= NOT(temporal);
                counter <= 0;
            else
                counter <= counter + 1;
            end if;
         end if;
    end process;
    
    clk_out <= temporal;
end behav;
